// Logisim project alu.circ as structural Verilog: 6 circuits, main circuit alu
module alu (
  input  [31:0] A,
  input  [31:0] B,
  input  [3:0] ALUSel,
  output [31:0] Result
);

  wire [31:0] add0, and1, mul10, mulh14, mulhu11, or2, sll6, slt7, sra5, srl4, sub12, xor3;

  Adder #(.width(32)) adder_1 (.a(A), .b(B), .out(add0));  // open: cin, cout
  assign and1 = A & B;  // AND_Gate and_1, 32 bits wide
  assign or2 = A | B;  // OR_Gate or_1, 32 bits wide
  assign xor3 = A ^ B;  // XOR_Gate xor_1, 32 bits wide
  Subtractor #(.width(32)) subtractor_1 (.a(A), .b(B), .out(sub12));  // open: bin, bout
  mysrl mysrl_1 (.inputA(A), .inputB(B), .output_srl(srl4));
  mysra mysra_1 (.inputA(A), .inputB(B), .output_sra(sra5));
  mysll mysll_1 (.inputA(A), .inputB(B), .output_sll(sll6));
  myslt myslt_1 (.inputA(A), .inputB(B), .output_slt(slt7));
  mymul mymul_1 (.inputA(A), .inputB(B), .output_mul(mul10), .output_muluh(mulhu11), .output_mulh(mulh14));
  Multiplexer #(.enable("false"), .select(4), .width(32)) multiplexer_1 (
    .in0(add0), .in1(and1), .in2(or2), .in3(xor3), .in4(srl4), .in5(sra5), .in6(sll6), .in7(slt7),
    .in10(mul10), .in11(mulhu11), .in12(sub12), .in13(B), .in14(mulh14), .out(Result), .sel(ALUSel));  // open: in8, in9, in15

  // Other names for the same wires on the sheet: bsel13[31:0] = B

  // Notes on the sheet:
  //   INPUTS to your circuit
  //   DON'T CHANGE THE LOCATIONS OF THE INPUTS AND OUTPUTS!
  //   OUTPUT from your circuit
endmodule

module mysrl (
  input  [31:0] inputA,
  input  [31:0] inputB,
  output [31:0] output_srl
);

  Shifter #(.shift("lr"), .width(32)) shifter_1 (.in(inputA), .\dist (inputB[4:0]), .out(output_srl));
endmodule

module mysra (
  input  [31:0] inputA,
  input  [31:0] inputB,
  output [31:0] output_sra
);

  Shifter #(.shift("ar"), .width(32)) shifter_1 (.in(inputA), .\dist (inputB[4:0]), .out(output_sra));
endmodule

module mysll (
  input  [31:0] inputA,
  input  [31:0] inputB,
  output [31:0] output_sll
);

  Shifter #(.width(32)) shifter_1 (.in(inputA), .\dist (inputB[4:0]), .out(output_sll));
endmodule

module myslt (
  input  [31:0] inputA,
  input  [31:0] inputB,
  output [31:0] output_slt
);

  Comparator #(.width(32)) comparator_1 (.a(inputA), .b(inputB), .lt(output_slt[0]));  // open: gt, eq

  assign output_slt[31:1] = {31{1'b0}};
endmodule

module mymul (
  input  [31:0] inputA,
  input  [31:0] inputB,
  output [31:0] output_mul,
  output [31:0] output_muluh,
  output [31:0] output_mulh
);

  Multiplier #(.width(32)) multiplier_1 (.a(inputA), .b(inputB), .out(output_mul), .cout(output_muluh));  // open: cin
  Multiplier #(.mode("twosComplement"), .width(32)) multiplier_2 (
    .a(inputA), .b(inputB), .cout(output_mulh));  // open: out, cin
endmodule
