// Logisim project control_logic.circ as structural Verilog: 1 circuit, main circuit control_logic
module control_logic (
  input  [31:0] inst,
  input  BrEq,
  input  BrLt,
  output PCSel,
  output RegWEn,
  output [2:0] ImmSel,
  output BrUn,
  output ASel,
  output BSel,
  output [3:0] ALUSel,
  output MemRW,
  output [1:0] WBSel,
  output CSRSel,
  output CSRWen
);

  wire and_2_out, auipc, branch, immALU, jalr, load, lui, multiplexer_1_out, multiplexer_2_out,
       multiplexer_3_out, nor_1_out, not_1_out, not_3_out, not_4_out, not_5_out, or_1_out, or_5_out,
       or_6_out, R_cmd;
  wire [3:0] multiplexer_4_out, rom_1_data, rom_2_data;

  or or_1 (or_1_out, lui, R_cmd, immALU, auipc);
  or or_2 (WBSel[0], jalr, inst[3], or_1_out);
  or or_3 (WBSel[1], or_1_out, CSRWen);
  or or_4 (RegWEn, WBSel[1], WBSel[0], load);
  or or_5 (or_5_out, load, immALU, jalr, CSRWen);
  or or_6 (or_6_out, auipc, lui);
  or or_7 (ImmSel[0], or_5_out, branch, inst[3]);
  or or_8 (ImmSel[1], MemRW, branch);
  or or_9 (ImmSel[2], inst[3], or_6_out);
  nor nor_1 (nor_1_out, inst[3], not_1_out);
  Demultiplexer #(.enable("false"), .select(2)) demultiplexer_1 (
    .out1(auipc), .out2(jalr), .out3(lui), .in(nor_1_out), .sel(inst[5:4]));  // open: out0
  not not_1 (not_1_out, inst[2]);
  Demultiplexer #(.enable("false"), .select(3)) demultiplexer_2 (
    .out0(load), .out1(immALU), .out2(MemRW), .out3(R_cmd), .out6(branch), .out7(CSRWen), .in(not_1_out),
    .sel(inst[6:4]));  // open: out4, out5
  ROM #(.addrWidth(5), .dataWidth(4)) rom_1 (.addr({inst[14:12], inst[30], inst[25]}), .data(rom_1_data));
  ROM #(.addrWidth(5), .dataWidth(4)) rom_2 (.addr({inst[14:12], inst[30], inst[25]}), .data(rom_2_data));
  not not_2 (BSel, R_cmd);
  or or_10 (ASel, auipc, jalr, inst[3], branch);
  not not_3 (not_3_out, inst[13]);
  and and_1 (CSRSel, inst[12], not_3_out, inst[14], CSRWen);
  not not_4 (not_4_out, BrEq);
  not not_5 (not_5_out, BrLt);
  Multiplexer #(.enable("false")) multiplexer_1 (.in0(BrEq), .in1(not_4_out), .out(multiplexer_1_out), .sel(inst[12]));
  Multiplexer #(.enable("false")) multiplexer_2 (
    .in0(multiplexer_1_out), .in1(multiplexer_3_out), .out(multiplexer_2_out), .sel(inst[14]));
  Multiplexer #(.enable("false")) multiplexer_3 (.in0(BrLt), .in1(not_5_out), .out(multiplexer_3_out), .sel(inst[12]));
  Multiplexer #(.enable("false"), .select(2), .width(4)) multiplexer_4 (
    .in0(4'b0000), .in1(rom_1_data), .in2(rom_2_data), .out(multiplexer_4_out), .sel({immALU, R_cmd}));  // open: in3
  Multiplexer #(.enable("false"), .width(4)) multiplexer_5 (
    .in0(multiplexer_4_out), .in1(4'b1101), .out(ALUSel), .sel(lui));
  and and_2 (and_2_out, branch, multiplexer_2_out);
  or or_11 (PCSel, and_2_out, inst[3], jalr);

  assign BrUn = inst[13];

  // Other names for the same wires on the sheet: op2 = inst[4]; opcode[6:0] = inst[6:0]; op3 = inst[5]; op4 = inst[6];
  //   func7[6:0] = inst[31:25]; func3[2:0] = inst[14:12]; csr_cmd = CSRWen; op0 = inst[2]; jal = inst[3];
  //   op1 = inst[3]; save = MemRW

  // Notes on the sheet:
  //   INPUTS to your circuit
  //   00 for sMEM, 01 for PC+4, 10 for sCSR, 11 for sALU
  //   DON'T CHANGE THE LOCATIONS OF THE INPUTS AND OUTPUTS!
  //   OUTPUT from your circuit
  //   000 R, 001 I, 010 S, 011 SB, 100 U, 101 UJ
  //   contents of rom_1 (hex, n*v repeats v):
  //   0 a c 0 6 e 0 0 7 4*0 b 0 0 3 0 0 0 4 0 5 0 2 0 0 0 1
  //   contents of rom_2 (hex, n*v repeats v):
  //   4*0 6 0 0 0 4*7 4*0 4*3 4 0 5 0 4*2 4*1
endmodule
