// Logisim project cpu.circ as structural Verilog: 5 circuits, main circuit cpu
module cpu (
  input  clk,
  input  [31:0] INSTRUCTION,
  input  [31:0] READ_DATA,
  output [31:0] WRITE_ADDRESS,
  output [31:0] PROGRAM_COUNTER,
  output [31:0] ra,
  output [31:0] sp,
  output [31:0] t0,
  output [31:0] t1,
  output [31:0] t2,
  output [31:0] s0,
  output [31:0] s1,
  output [31:0] a0,
  output [31:0] tohost,
  output [3:0] WRITE_ENABLE,
  output [31:0] WRITE_DATA,
  output [31:0] out_17,
  output [31:0] out_18,
  output [3:0] out_19
);

  wire ASel, BrEq, BrLt, BrUn, BSel, CSRSel, CSRWen, MemRW, PCSel, RegWEn;
  wire [1:0] WBSel;
  wire [2:0] ImmSel;
  wire [4:0] rd, rs1, rs2;
  wire [11:0] addr_CSR;
  wire [31:0] adder_1_out, data_CSR, inst2, multiplexer_1_out, multiplexer_2_out, multiplexer_3_out,
       multiplexer_4_out, PC2, rs1_data, WB_data;

  Adder #(.width(32)) adder_1 (.a(PROGRAM_COUNTER), .b(32'h4), .out(adder_1_out));  // open: cin, cout
  Register #(.width(32)) PC (.D(multiplexer_1_out), .clk(clk), .Q(PROGRAM_COUNTER));  // open: en, clr
  Multiplexer #(.enable("false"), .width(32)) multiplexer_1 (
    .in0(adder_1_out), .in1(out_18), .out(multiplexer_1_out), .sel(PCSel));
  Register #(.width(32)) register_1 (.D(PROGRAM_COUNTER), .clk(clk), .Q(PC2));  // open: en, clr
  Register #(.width(32)) register_2 (.D(multiplexer_2_out), .clk(clk), .Q(inst2));  // open: en, clr
  Multiplexer #(.enable("false"), .width(32)) multiplexer_2 (
    .in0(INSTRUCTION), .in1(32'h13), .out(multiplexer_2_out), .sel(PCSel));
  control_logic control_logic_1 (
    .CSRWen(CSRWen), .PCSel(PCSel), .RegWEn(RegWEn), .ImmSel(ImmSel), .BrUn(BrUn), .ASel(ASel), .BSel(BSel),
    .ALUSel(out_19), .MemRW(MemRW), .WBSel(WBSel), .CSRSel(CSRSel), .inst(inst2), .BrEq(BrEq), .BrLt(BrLt));
  imm_gen imm_gen_1 (.inst(inst2), .ImmSel(ImmSel), .imm(out_17));
  inst_reg inst_reg_1 (.inst(inst2), .rd(rd), .rs1(rs1), .rs2(rs2));
  regfile regfile_1 (
    .rs1(rs1), .rs2(rs2), .rd(rd), .Write_Data(WB_data), .RegWEn(RegWEn), .clk(clk), .ra(ra), .sp(sp),
    .t0(t0), .t1(t1), .t2(t2), .s0(s0), .s1(s1), .a0(a0), .Read_Data_1(rs1_data), .Read_Data_2(WRITE_DATA));
  branch_comp branch_comp_1 (.rs1(rs1_data), .rs2(WRITE_DATA), .BrUn(BrUn), .BrEq(BrEq), .BrLt(BrLt));
  CSRprocess csrprocess_1 (
    .is_imm(CSRSel), .rs1_data(rs1_data), .inst(inst2), .data_CSR(data_CSR), .addr_CSR(addr_CSR));
  Multiplexer #(.enable("false"), .width(32)) multiplexer_3 (
    .in0(rs1_data), .in1(PC2), .out(multiplexer_3_out), .sel(ASel));
  Multiplexer #(.enable("false"), .width(32)) multiplexer_4 (
    .in0(WRITE_DATA), .in1(out_17), .out(multiplexer_4_out), .sel(BSel));
  alu alu_1 (.Result(out_18), .A(multiplexer_3_out), .B(multiplexer_4_out), .ALUSel(out_19));
  csr csr_1 (.CSR_address(addr_CSR), .CSR_din(data_CSR), .CSR_WE(CSRWen), .clk(clk), .tohost(tohost));
  write_back write_back_1 (
    .Mem_data(READ_DATA), .PCaft(PROGRAM_COUNTER), .CSR_data(tohost), .ALU_res(out_18), .WBSel(WBSel),
    .write_data(WB_data));
  DMEM_process dmem_process_1 (.ALU_res(out_18), .RW(MemRW), .inst(inst2), .addr(WRITE_ADDRESS), .Wen(WRITE_ENABLE));

  // Other names for the same wires on the sheet: ALUSel[3:0] = out_19; imm[31:0] = out_17; res[31:0] = out_18;
  //   rs2_data[31:0] = WRITE_DATA

  // Notes on the sheet:
  //   Output to IMEM
  //   IMEM (do **NOT** move this)
  //   Inputs from IMEM
  //   It is OK to move the PC, RegFile, ALU, MEM, Branch Comp, Imm Gen, and Control Logic to wherever is most convenient for you when constructing your CPU, and to delete this text
  //   Inputs/Outputs for testing. Do **NOT** move these.
  //   Outputs To DMEM
  //   DMEM (do **NOT** move this)
  //   Inputs From DMEM
endmodule

module inst_reg (
  input  [31:0] inst,
  output [4:0] rd,
  output [4:0] rs1,
  output [4:0] rs2
);


  assign rd = inst[11:7];
  assign rs1 = inst[19:15];
  assign rs2 = inst[24:20];
endmodule

module write_back (
  input  [31:0] Mem_data,
  input  [31:0] PCaft,
  input  [31:0] CSR_data,
  input  [31:0] ALU_res,
  input  [1:0] WBSel,
  output [31:0] write_data
);

  wire [31:0] multiplexer_1_out, multiplexer_2_out;

  Multiplexer #(.enable("false"), .width(32)) multiplexer_1 (
    .in0(CSR_data), .in1(ALU_res), .out(multiplexer_1_out), .sel(WBSel[0]));
  Multiplexer #(.enable("false"), .width(32)) multiplexer_2 (
    .in0(Mem_data), .in1(PCaft), .out(multiplexer_2_out), .sel(WBSel[0]));
  Multiplexer #(.enable("false"), .width(32)) multiplexer_3 (
    .in0(multiplexer_2_out), .in1(multiplexer_1_out), .out(write_data), .sel(WBSel[1]));
endmodule

module CSRprocess (
  input  is_imm,
  input  [31:0] rs1_data,
  input  [31:0] inst,
  output [31:0] data_CSR,
  output [11:0] addr_CSR
);

  Multiplexer #(.enable("false"), .width(32)) multiplexer_1 (
    .in0(rs1_data), .in1({{27{1'b0}}, inst[19:15]}), .out(data_CSR), .sel(is_imm));

  assign addr_CSR = inst[31:20];
endmodule

module DMEM_process (
  input  [31:0] ALU_res,
  input  RW,
  input  [31:0] inst,
  output [31:0] addr,
  output [3:0] Wen
);

  wire [3:0] multiplexer_1_out, multiplexer_2_out, multiplexer_3_out;

  Multiplexer #(.enable("false"), .select(2), .width(4)) multiplexer_1 (
    .in0(4'b0001), .in1(4'b0010), .in2(4'b0100), .in3(4'b1000), .out(multiplexer_1_out), .sel(ALU_res[4:3]));
  Multiplexer #(.enable("false"), .width(4)) multiplexer_2 (
    .in0(4'b0011), .in1(4'b1100), .out(multiplexer_2_out), .sel(ALU_res[4]));
  Multiplexer #(.enable("false"), .select(2), .width(4)) multiplexer_3 (
    .in0(multiplexer_1_out), .in1(multiplexer_2_out), .in2(4'b1111), .out(multiplexer_3_out),
    .sel(inst[13:12]));  // open: in3
  Multiplexer #(.enable("false"), .width(4)) multiplexer_4 (
    .in0(4'b0000), .in1(multiplexer_3_out), .out(Wen), .sel(RW));

  assign addr = ALU_res;
endmodule
