// Logisim project imm_gen.circ as structural Verilog: 6 circuits, main circuit imm_gen
module imm_gen (
  input  [31:0] inst,
  input  [2:0] ImmSel,
  output [31:0] imm
);

  wire [31:0] i_imm_gen_1_i_imm, s_imm_gen_1_s_imm, sb_imm_gen_1_sb_imm, u_imm_gen_1_u_imm,
       uj_imm_gen_1_u_imm;

  I_imm_gen i_imm_gen_1 (.inst(inst), .I_imm(i_imm_gen_1_i_imm));
  S_imm_gen s_imm_gen_1 (.inst(inst), .S_imm(s_imm_gen_1_s_imm));
  SB_imm_gen sb_imm_gen_1 (.inst(inst), .SB_imm(sb_imm_gen_1_sb_imm));
  U_imm_gen u_imm_gen_1 (.inst(inst), .U_imm(u_imm_gen_1_u_imm));
  UJ_imm_gen uj_imm_gen_1 (.inst(inst), .U_imm(uj_imm_gen_1_u_imm));
  Multiplexer #(.enable("false"), .select(3), .width(32)) multiplexer_1 (
    .in1(i_imm_gen_1_i_imm), .in2(s_imm_gen_1_s_imm), .in3(sb_imm_gen_1_sb_imm), .in4(u_imm_gen_1_u_imm),
    .in5(uj_imm_gen_1_u_imm), .out(imm), .sel(ImmSel));  // open: in0, in6, in7

  // Notes on the sheet:
  //   INPUTS to your circuit
  //   DON'T CHANGE THE LOCATIONS OF THE INPUTS AND OUTPUTS!
  //   OUTPUT from your circuit
endmodule

module I_imm_gen (
  input  [31:0] inst,
  output [31:0] I_imm
);

  assign I_imm = {{20{inst[31]}}, inst[31:20]};  // Bit_Extender bit_extender_1
endmodule

module S_imm_gen (
  input  [31:0] inst,
  output [31:0] S_imm
);

  assign S_imm = {{20{inst[31]}}, {inst[31:25], inst[11:7]}};  // Bit_Extender bit_extender_1
endmodule

module SB_imm_gen (
  input  [31:0] inst,
  output [31:0] SB_imm
);

  assign SB_imm[31:13] = {{18{inst[31]}}, inst[31]};  // Bit_Extender bit_extender_1

  assign SB_imm[12:0] = {inst[31], inst[7], inst[30:25], inst[11:8], 1'b0};
endmodule

module U_imm_gen (
  input  [31:0] inst,
  output [31:0] U_imm
);


  assign U_imm = {inst[31:12], {12{1'b0}}};
endmodule

module UJ_imm_gen (
  input  [31:0] inst,
  output [31:0] U_imm
);

  assign U_imm = {{12{inst[31]}}, {inst[31], inst[19:12], inst[20], inst[30:21]}};  // Bit_Extender bit_extender_1
endmodule
